# Fritzing sketch circuit (saved by Fritzing 0.9.2b)
circuit board: 3.25159cm x 2.78818cm
stripboards: 1

parts:
  U1 = ESP8266 WiFi Module [part_number=ESP8266]
  REG1 = LD33 Low-Dropout Voltage Regulator
  R1 = Resistor [tolerance=±5% resistance=4.7k package=THT]
  DS1 = DS18B20 1-Wire Temperature Sensor [part_number=DS18B20]
  Power_plug1 = Power plug

nets:
  VCC: U1.VCC, U1.CH_PD, REG1.Vout, R1.Pin_0, DS1.VDD
  N1: U1.GPIO_0, R1.Pin_1, DS1.DQ
  GND: U1.GND, REG1.GND, DS1.GND, Power_plug1.GND
  VIN: REG1.Vin, Power_plug1.VCC

custom parts:
  ESP8266 WiFi Module: Generic WiFi Module based on the ESP8266 with onboard PCB antenna and UART communications
